# Fritzing sketch Iot_101 (saved by Fritzing 0.9.2b)
breadboards: 1

parts:
  Raspberry_Pi1 = Raspberry Pi 2
  LED1 = LED - 3mm [color="Red (633nm)" package="3 mm [THT]"]
  R1 = Resistor [tolerance=±5% resistance=470 package="2010 [SMD]"]
  R2 = Resistor [tolerance=±5% resistance=470 package="1206 [SMD]"]
  R3 = Resistor [tolerance=±5% resistance=1k package="1206 [SMD]"]

nets:
  N1: Raspberry_Pi1.3v3, R3.Pin_1
  N2: Raspberry_Pi1.GPIO17, R1.Pin_1
  N3: Raspberry_Pi1.GPIO27, R2.Pin_1, R3.Pin_0
  N4: Raspberry_Pi1.GND, LED1.cathode, R2.Pin_0
  N5: LED1.anode, R1.Pin_0
